# Fritzing sketch DiagramaElectroMecanico (saved by Fritzing 0.9.3b)

parts:
  Componente1 = Arduino Uno (Rev3)
  S1 = H-Bridge with L298N
  M1 = DC Motor  # not connected
  M2 = DC Motor
  VCC1 = Battery
  Componente3 = Bluetooth HC-06

nets:
  N1: Componente1.D9_PWM, S1.IN2
  N2: Componente1.D10_PWM/SS, S1.IN1
  N3: Componente1.D0/RX, Componente3.TXD
  N4: Componente1.D1/TX, Componente3.RXD
  N5: Componente1.D5_PWM, S1.IN4
  N6: Componente1.D6_PWM, S1.IN3
  5V: Componente1.5V, S1.5V, Componente3.VCC
  GND: Componente1.GND, VCC1.-, Componente3.GND
  N7: S1.12V, VCC1.+
  N8: S1.OUT4-Motor2, M2.pin_1

custom parts:
  H-Bridge with L298N: h-bridge
  Battery: Your standard 2x 18650 battery pack (7,4 Volts)
